# Fritzing sketch A321 (saved by Fritzing 0.9.7b)

parts:
  Baro = Rotary Encoder [package=THT]
  Hg/HPa = Toggle Switch [package=THT]
  CRST = Round Pushbutton
  WPT = Round Pushbutton
  VORD = Round Pushbutton
  NAV = Round Pushbutton
  LOC = Round Pushbutton
  ARPT = Round Pushbutton
  FD = Round Pushbutton
  LS = Round Pushbutton
  Master = Round Pushbutton
  Chrono = Round Pushbutton
  Warning = Round Pushbutton
  com1 = Toggle Switch [package=THT]
  com2 = Toggle Switch [package=THT]
  APPR = Round Pushbutton
  Strobe = Toggle Switch [package=THT]
  Rwy_Turn_Off = Toggle Switch [package=THT]
  Wing = Toggle Switch [package=THT]
  Nav = Toggle Switch [package=THT]
  Seatbelt = Toggle Switch [package=THT]
  Land_2 = Toggle Switch [package=THT]
  Land_1 = Toggle Switch [package=THT]
  Nose = Toggle Switch [package=THT]
  STD = Round Pushbutton
  D1 = Diode [package=diode-1n4001]
  D2 = Diode [package=diode-1n4001]
  D3 = Diode [package=diode-1n4001]
  D4 = Diode [package=diode-1n4001]
  D5 = Diode [package=diode-1n4001]
  D7 = Diode [package=diode-1n4001]
  D8 = Diode [package=diode-1n4001]
  D9 = Diode [package=diode-1n4001]
  D10 = Diode [package=diode-1n4001]
  D11 = Diode [package=diode-1n4001]
  D12 = Diode [package=diode-1n4001]
  Beacon = Toggle Switch [package=THT]
  D13 = Diode [package=diode-1n4001]
  D14 = Diode [package=diode-1n4001]
  D15 = Diode [package=diode-1n4001]
  D16 = Diode [package=diode-1n4001]
  D17 = Diode [package=diode-1n4001]
  D18 = Diode [package=diode-1n4001]
  D19 = Diode [package=diode-1n4001]
  D20 = Diode [package=diode-1n4001]
  D21 = Diode [package=diode-1n4001]
  D22 = Diode [package=diode-1n4001]
  D23 = Diode [package=diode-1n4001]
  D24 = Diode [package=diode-1n4001]
  D25 = Diode [package=diode-1n4001]
  D26 = Diode [package=diode-1n4001]
  D27 = Diode [package=diode-1n4001]
  D28 = Diode [package=diode-1n4001]
  D29 = Diode [package=diode-1n4001]
  Brightness = Rotary Encoder [package=THT]
  unassigned = Round Pushbutton
  D38 = Diode [package=diode-1n4001]
  ND = Rotary_Switch_12x1
  D39 = Diode [package=diode-1n4001]
  D40 = Diode [package=diode-1n4001]
  D41 = Diode [package=diode-1n4001]
  D42 = Diode [package=diode-1n4001]
  D44 = Diode [package=diode-1n4001]
  D45 = Diode [package=diode-1n4001]
  D46 = Diode [package=diode-1n4001]
  D47 = Diode [package=diode-1n4001]
  D48 = Diode [package=diode-1n4001]
  Range = Rotary_Switch_12x1
  D6 = Diode [package=diode-1n4001]
  Teensy1 = Teensy 4.1

nets (from the schematic view):
  N1: Baro.EncoderPinA, Teensy1.D8
  N2: Baro.EncoderPinC, Teensy1.D9
  N3: Baro.EncoderPinB, Teensy1.D10
  N4: Hg/HPa.L1, D7.A
  N5: Hg/HPa.COM, com2.COM, APPR.leg1, unassigned.leg1, Teensy1.A2/D16
  N6: CRST.leg0, D8.A
  N7: CRST.leg1, Warning.leg1, Land_2.COM, Beacon.COM, Teensy1.A8/D22
  N8: WPT.leg0, D9.A
  N9: WPT.leg1, Master.leg1, Strobe.COM, Land_1.COM, Teensy1.A7/D21
  N10: VORD.leg0, D10.A
  N11: VORD.leg1, Chrono.leg1, Wing.COM, Nose.COM, Teensy1.A6/D20
  N12: NAV.leg0, D11.A
  N13: NAV.leg1, FD.leg1, Rwy_Turn_Off.COM, Nav.COM, Teensy1.A5/D19
  N14: LOC.leg0, D17.A
  N15: LOC.leg1, com1.COM, STD.leg1, Teensy1.A3/D17
  N16: ARPT.leg0, D12.A
  N17: ARPT.leg1, LS.leg1, Seatbelt.COM, Teensy1.A4/D18
  N18: FD.leg0, D4.A
  N19: LS.leg0, D5.A
  N20: Master.leg0, D2.A
  N21: Chrono.leg0, D3.A
  N22: Warning.leg0, D1.A
  N23: com1.L1, D15.A
  N24: com2.L1, D16.A
  N25: APPR.leg0, D18.A
  N26: Strobe.L1, D14.A
  N27: Rwy_Turn_Off.L1, D19.A
  N28: Wing.L1, D24.A
  N29: Nav.L1, D28.A
  N30: Nav.L2, D27.A
  N31: Seatbelt.L1, D29.A
  N32: Land_2.L1, D21.A
  N33: Land_2.L2, D20.A
  N34: Land_1.L1, D23.A
  N35: Land_1.L2, D22.A
  N36: Nose.L1, D26.A
  N37: Nose.L2, D25.A
  N38: STD.leg0, D6.A
  N39: D1.C, D2.C, D3.C, D4.C, D5.C, D7.C, D40.C, D46.C, D6.C, Teensy1.D4
  N40: D8.C, D9.C, D10.C, D11.C, D12.C, D17.C, D18.C, D39.C, D48.C, Teensy1.D3
  N41: Beacon.L1, D13.A
  N42: D13.C, D14.C, D15.C, D16.C, D19.C, D24.C, D29.C, D41.C, D47.C, Teensy1.D2
  N43: D20.C, D22.C, D25.C, D27.C, D38.C, D42.C, D44.C, Teensy1.D1
  N44: D21.C, D23.C, D26.C, D28.C, D45.C, Teensy1.D0
  N45: Brightness.EncoderPinA, Teensy1.D5
  N46: Brightness.EncoderPinC, Teensy1.D6
  N47: Brightness.EncoderPinB, Teensy1.D7
  N48: unassigned.leg0, D38.A
  N49: ND.0, Teensy1.A1/D15
  N50: ND.1, D40.A, D46.A, Range.1
  N51: ND.2, ND.3, ND.4, ND.5, D39.A, D41.A, D42.A, D44.A, D45.A, D47.A, D48.A, Range.2, Range.3, Range.4, Range.5
  N52: Range.0, Teensy1.A0/D14

custom parts:
  Teensy 4.1: The Teensy is a complete USB-based microcontoller development system, in a very small footprint, capable of implementing many types of projects. All programming is done via the USB port. No special programmer is needed, only a standard micro-USB cable and a PC or Macintosh with a USB port.
